// Logisim project Karnaugh map.circ as structural Verilog: 4 circuits, main circuit main
module main (
  input  W,
  input  X,
  input  Y,
  input  Z,
  output out_5,
  output C_Y_prime_Z_prime_YZ,
  output out_7,
  output out_8
);

  wire ic7404_1_out_7, ic7404_1_out_9, ic7404_1_out_10, ic7411_1_out_10, ic7411_1_out_11, ic7411_1_out_12,
       ic7411_2_out_10, ic7411_2_out_11, ic7411_2_out_12;

  IC7411 ic7411_1 (
    .in_1(ic7404_1_out_7), .in_2(Z), .in_4(X), .in_5(Y), .in_7(X), .in_8(Z), .out_10(ic7411_1_out_10),
    .out_11(ic7411_1_out_11), .out_12(ic7411_1_out_12));  // open: in_3, in_6, in_9
  IC4075 ic4075_1 (
    .in_4(W), .in_5(ic7411_1_out_12), .in_6(ic7411_1_out_11), .in_7(ic7411_1_out_10), .in_8(ic7411_2_out_11),
    .in_9(ic7411_2_out_10), .out_11(out_7), .out_12(out_5));  // open: in_1, in_2, in_3, out_10
  IC7404 ic7404_1 (
    .in_1(X), .in_2(Z), .in_3(Y), .in_4(ic7411_2_out_12), .out_7(ic7404_1_out_7), .out_8(out_8),
    .out_9(ic7404_1_out_9), .out_10(ic7404_1_out_10));  // open: in_5, in_6, out_11, out_12
  IC7411 ic7411_2 (
    .in_1(X), .in_2(ic7404_1_out_9), .in_3(out_8), .in_4(Y), .in_5(ic7404_1_out_7), .in_7(Y), .in_8(Z),
    .out_10(ic7411_2_out_10), .out_11(ic7411_2_out_11), .out_12(ic7411_2_out_12));  // open: in_6, in_9
  IC4075 ic4075_2 (
    .in_4(ic7411_2_out_12), .in_5(ic7404_1_out_10), .out_11(C_Y_prime_Z_prime_YZ));  // open: in_1, in_2, in_3, in_6, in_7, in_8, in_9, out_10, out_12

  // Notes on the sheet:
  //   XY
  //   XZ
  //   X'
  //   Z'
  //   Y'
  //   X'Z
  //   B=X'Z+X'Y+XY'Z'
  //   A=W+XZ+XY
  //   X'Y
  //   YZ
  //   Y'Z'
  //   XY'Z'
  //   D=Z'
endmodule

module IC7404 (
  input  in_1,
  input  in_2,
  input  in_3,
  input  in_4,
  input  in_5,
  input  in_6,
  output out_7,
  output out_8,
  output out_9,
  output out_10,
  output out_11,
  output out_12
);

  not not_1 (out_7, in_1);
  not not_2 (out_8, in_2);
  not not_3 (out_9, in_3);
  not not_4 (out_10, in_4);
  not not_5 (out_11, in_5);
  not not_6 (out_12, in_6);
endmodule

module IC7411 (
  input  in_1,
  input  in_2,
  input  in_3,
  input  in_4,
  input  in_5,
  input  in_6,
  input  in_7,
  input  in_8,
  input  in_9,
  output out_10,
  output out_11,
  output out_12
);

  and and_1 (out_10, in_1, in_2, in_3);
  and and_2 (out_11, in_4, in_5, in_6);
  and and_3 (out_12, in_7, in_8, in_9);
endmodule

module IC4075 (
  input  in_1,
  input  in_2,
  input  in_3,
  input  in_4,
  input  in_5,
  input  in_6,
  input  in_7,
  input  in_8,
  input  in_9,
  output out_10,
  output out_11,
  output out_12
);

  or or_1 (out_10, in_1, in_2, in_3);
  or or_2 (out_11, in_4, in_5, in_6);
  or or_3 (out_12, in_7, in_8, in_9);
endmodule
