// Logisim project Week05task1.circ as structural Verilog: 3 circuits, main circuit main
module main (
  input  A1,
  input  A2,
  input  A3,
  input  A4,
  input  B1,
  input  B2,
  input  B3,
  input  B4,
  input  Cin,
  output Cout,
  output [3:0] out_11
);

  wire IC7486_out_9, IC7486_out_10, IC7486_out_11, IC7486_out_12;

  IC7486 IC7486 (
    .in_1(B1), .in_3(B2), .in_5(B3), .in_7(B4), .out_9(IC7486_out_9), .out_10(IC7486_out_10),
    .out_11(IC7486_out_11), .out_12(IC7486_out_12), .in_8(Cin), .in_6(Cin), .in_4(Cin), .in_2(Cin));
  _4_bit_adder_subtractor u_4_bit_adder_subtractor_1 (
    .in_2(A4), .in_4(A3), .in_6(A2), .in_7(IC7486_out_10), .in_8(A1), .in_9(IC7486_out_9), .out_10(out_11),
    .in_5(IC7486_out_11), .in_3(IC7486_out_12), .in_1(Cin), .out_11(Cout));
endmodule

module IC7486 (
  input  in_1,
  input  in_2,
  input  in_3,
  input  in_4,
  input  in_5,
  input  in_6,
  input  in_7,
  input  in_8,
  output out_9,
  output out_10,
  output out_11,
  output out_12
);

  xor xor_1 (out_9, in_1, in_2);
  xor xor_2 (out_10, in_3, in_4);
  xor xor_3 (out_11, in_5, in_6);
  xor xor_4 (out_12, in_7, in_8);
endmodule

module _4_bit_adder_subtractor (
  input  in_1,
  input  in_2,
  input  in_3,
  input  in_4,
  input  in_5,
  input  in_6,
  input  in_7,
  input  in_8,
  input  in_9,
  output [3:0] out_10,
  output out_11
);

  wire adder_1_cout, adder_2_cout, adder_3_cout;

  Adder #(.width(1)) adder_1 (.a(in_2), .b(in_3), .out(out_10[0]), .cin(in_1), .cout(adder_1_cout));
  Adder #(.width(1)) adder_2 (.a(in_4), .b(in_5), .out(out_10[1]), .cin(adder_1_cout), .cout(adder_2_cout));
  Adder #(.width(1)) adder_3 (.a(in_6), .b(in_7), .out(out_10[2]), .cin(adder_2_cout), .cout(adder_3_cout));
  Adder #(.width(1)) adder_4 (.a(in_8), .b(in_9), .out(out_10[3]), .cin(adder_3_cout), .cout(out_11));
endmodule
