// Logisim project week5task2.circ as structural Verilog: 4 circuits, main circuit main
module main (
  input  A0,
  input  A1,
  input  A2,
  input  A3,
  input  B0,
  input  B1,
  input  B2,
  input  B3,
  input  Cin,
  input  in_10,
  input  in_11,
  output Cout
);

  wire ic7408_1_out_11, ic7408_1_out_12, ic7432_1_out_10, ic7432_1_out_11, ic74283_1_out_10,
       ic74283_1_out_11, ic74283_1_out_12, ic74283_1_out_13, ic74283_2_out_10, ic74283_2_out_11,
       ic74283_2_out_12, ic74283_2_out_13;

  IC7432 ic7432_1 (
    .in_3(ic7432_1_out_11), .in_4(Cout), .in_5(ic7408_1_out_12), .in_6(ic7408_1_out_11),
    .out_10(ic7432_1_out_10), .out_11(ic7432_1_out_11));  // open: in_1, in_2, in_7, in_8, out_9, out_12
  IC7408 ic7408_1 (
    .in_5(ic74283_1_out_11), .in_6(ic74283_1_out_13), .in_7(ic74283_1_out_13), .in_8(ic74283_1_out_12),
    .out_11(ic7408_1_out_11), .out_12(ic7408_1_out_12));  // open: in_1, in_2, in_3, in_4, out_9, out_10
  IC74283 ic74283_1 (
    .in_1(Cin), .in_2(A0), .in_3(B0), .in_4(A1), .in_5(B1), .in_6(A2), .in_7(B2), .in_8(A3), .in_9(B3),
    .out_14(Cout), .out_10(ic74283_1_out_10), .out_11(ic74283_1_out_11), .out_12(ic74283_1_out_12),
    .out_13(ic74283_1_out_13));
  IC74283 ic74283_2 (
    .in_1(in_11), .in_2(in_10), .in_3(ic74283_1_out_10), .in_4(ic7432_1_out_10), .in_5(ic74283_1_out_11),
    .in_6(ic7432_1_out_10), .in_7(ic74283_1_out_12), .in_8(in_10), .in_9(ic74283_1_out_13),
    .out_10(ic74283_2_out_10), .out_11(ic74283_2_out_11), .out_12(ic74283_2_out_12), .out_13(ic74283_2_out_13));  // open: out_14
  LED led_1 (.in(ic74283_2_out_10));
  LED led_2 (.in(ic74283_2_out_11));
  LED led_3 (.in(ic74283_2_out_12));
  LED led_4 (.in(ic74283_2_out_13));

  // Notes on the sheet:
  //   S0
  //   S1
  //   S2
  //   S3
endmodule

module IC74283 (
  input  in_1,
  input  in_2,
  input  in_3,
  input  in_4,
  input  in_5,
  input  in_6,
  input  in_7,
  input  in_8,
  input  in_9,
  output out_10,
  output out_11,
  output out_12,
  output out_13,
  output out_14
);

  wire adder_1_cout, adder_2_cout, adder_3_cout;

  Adder #(.width(1)) adder_1 (.a(in_2), .b(in_3), .out(out_10), .cin(in_1), .cout(adder_1_cout));
  Adder #(.width(1)) adder_2 (.a(in_4), .b(in_5), .out(out_11), .cin(adder_1_cout), .cout(adder_2_cout));
  Adder #(.width(1)) adder_3 (.a(in_6), .b(in_7), .out(out_12), .cin(adder_2_cout), .cout(adder_3_cout));
  Adder #(.width(1)) adder_4 (.a(in_8), .b(in_9), .out(out_13), .cin(adder_3_cout), .cout(out_14));
endmodule

module IC7408 (
  input  in_1,
  input  in_2,
  input  in_3,
  input  in_4,
  input  in_5,
  input  in_6,
  input  in_7,
  input  in_8,
  output out_9,
  output out_10,
  output out_11,
  output out_12
);

  and and_1 (out_9, in_1, in_2);
  and and_2 (out_10, in_3, in_4);
  and and_3 (out_11, in_5, in_6);
  and and_4 (out_12, in_7, in_8);
endmodule

module IC7432 (
  input  in_1,
  input  in_2,
  input  in_3,
  input  in_4,
  input  in_5,
  input  in_6,
  input  in_7,
  input  in_8,
  output out_9,
  output out_10,
  output out_11,
  output out_12
);

  or or_1 (out_9, in_1, in_2);
  or or_2 (out_10, in_3, in_4);
  or or_3 (out_11, in_5, in_6);
  or or_4 (out_12, in_7, in_8);
endmodule
