// Logisim project WEEK6TASK2.circ as structural Verilog: 1 circuit, main circuit main
module main (
  input  I0,
  input  D,
  input  I3,
  input  I4,
  input  I5,
  input  [2:0] ABC,
  input  I6,
  input  I7,
  input  in_9,
  output out_10
);

  Multiplexer #(.select(3), .enable("false")) multiplexer_1 (
    .in0(I0), .in1(D), .in2(D), .in3(I3), .in4(I4), .in5(I5), .in6(I6), .in7(I7), .out(out_10), .sel(ABC));
endmodule
