// Logisim project Week6Decoder.circ as structural Verilog: 1 circuit, main circuit main
module main (
  input  in_1,
  input  [2:0] in_2,
  output [7:0] out_3
);

  wire decoder_1_out0, decoder_1_out1, decoder_1_out2, decoder_1_out3, decoder_1_out4, decoder_1_out5,
       decoder_1_out6, decoder_1_out7;

  Decoder #(.select(3)) decoder_1 (
    .out0(decoder_1_out0), .out1(decoder_1_out1), .out2(decoder_1_out2), .out3(decoder_1_out3),
    .out4(decoder_1_out4), .out5(decoder_1_out5), .out6(decoder_1_out6), .out7(decoder_1_out7), .sel(in_2),
    .en(in_1));
  not not_1 (out_3[0], decoder_1_out0);
  not not_2 (out_3[1], decoder_1_out1);
  not not_3 (out_3[2], decoder_1_out2);
  not not_4 (out_3[3], decoder_1_out3);
  not not_5 (out_3[4], decoder_1_out4);
  not not_6 (out_3[5], decoder_1_out5);
  not not_7 (out_3[6], decoder_1_out6);
  not not_8 (out_3[7], decoder_1_out7);
endmodule
